# Fritzing sketch simon-says-arduino (saved by Fritzing 0.9.3b)
breadboards: 1

parts:
  S1 = Pushbutton [package="[THT]"]
  R1 = Resistor [tolerance=±5% resistance=220 package=THT]
  R2 = Resistor [tolerance=±5% resistance=10k package=THT]
  Part1 = Arduino Uno (Rev3)
  LED1 = LED - 5mm [color="Blue (470nm)" package="5 mm [THT]"]
  S2 = Pushbutton [package="[THT]"]
  S3 = Pushbutton [package="[THT]"]
  S4 = Pushbutton [package="[THT]"]
  LED2 = LED - 5mm [color="Red (635nm)" package="5 mm [THT]"]
  LED3 = LED - 5mm [color="Yellow (585nm)" package="5 mm [THT]"]
  LED4 = LED - 5mm [color="Green (555nm)" package="5 mm [THT]"]
  R3 = Resistor [tolerance=±5% resistance=10k package=THT]
  R4 = Resistor [tolerance=±5% resistance=10k package=THT]
  R5 = Resistor [tolerance=±5% resistance=10k package=THT]
  R6 = Resistor [tolerance=±5% resistance=220 package=THT]
  R7 = Resistor [tolerance=±5% resistance=220 package=THT]
  R8 = Resistor [tolerance=±5% resistance=220 package=THT]

nets:
  N1: S1.Pin_1, S1.Pin_2, Part1.D3_PWM, LED1.anode
  N2: S1.Pin_3, S1.Pin_4, Part1.5V, S2.Pin_3, S2.Pin_4, S3.Pin_3, S3.Pin_4, S4.Pin_3, S4.Pin_4
  N3: R1.Pin_0, R2.Pin_0, Part1.GND, R3.Pin_0, R4.Pin_0, R5.Pin_0, R6.Pin_0, R8.Pin_0
  N4: R1.Pin_1, LED1.cathode
  N5: R2.Pin_1, Part1.D2
  N6: Part1.D8, S4.Pin_1, S4.Pin_2, R5.Pin_1
  N7: Part1.D9_PWM, LED4.anode
  N8: Part1.D4, S2.Pin_1, S2.Pin_2, R3.Pin_1
  N9: Part1.D5_PWM, LED2.anode
  N10: Part1.D6_PWM, S3.Pin_1, S3.Pin_2, R4.Pin_1
  N11: Part1.D7, LED3.anode
  N12: LED2.cathode, R6.Pin_1
  N13: LED3.cathode, R7.Pin_1
  N14: LED4.cathode, R8.Pin_1
